// Logisim project control-logic.circ as structural Verilog: 1 circuit, main circuit control_logic
module control_logic (
  input  [31:0] inst,
  input  BrEq,
  input  BrLt,
  output PCSel,
  output RegWEn,
  output [2:0] ImmSel,
  output BrUn,
  output ASel,
  output BSel,
  output [3:0] ALUSel,
  output MemRW,
  output [1:0] WBSel,
  output CSRSel,
  output CSRWen
);

  wire comparator_2_eq, comparator_3_eq, comparator_4_eq, comparator_5_eq, comparator_6_eq, comparator_7_eq,
       comparator_8_eq, comparator_9_eq;
  wire [1:0] i;
  wire [5:0] priority_encoder_1_out;
  wire [7:0] addi, andi, ori, slli, slti, srai, srli, xori;
  wire [7:3] func3;
  wire [7:4] undriven;
  wire [7:7] opcode;
  wire [15:0] rom_1_data;

  Comparator comparator_1 (.a({opcode[7], inst[6:0]}), .b({undriven, 4'b1011}), .eq(i[0]));  // open: gt, lt
  Comparator comparator_2 (.a({func3, inst[14:12]}), .b({8{1'b0}}), .eq(comparator_2_eq));  // open: gt, lt
  Comparator comparator_3 (.a({func3, inst[14:12]}), .b(8'h1), .eq(comparator_3_eq));  // open: gt, lt
  Comparator comparator_4 (.a({func3, inst[14:12]}), .b(8'h2), .eq(comparator_4_eq));  // open: gt, lt
  Comparator comparator_5 (.a({func3, inst[14:12]}), .b(8'h4), .eq(comparator_5_eq));  // open: gt, lt
  Comparator comparator_6 (.a({func3, inst[14:12]}), .b(8'h5), .eq(comparator_6_eq));  // open: gt, lt
  Comparator comparator_7 (.a({func3, inst[14:12]}), .b(8'h5), .eq(comparator_7_eq));  // open: gt, lt
  Comparator comparator_8 (.a({func3, inst[14:12]}), .b(8'h6), .eq(comparator_8_eq));  // open: gt, lt
  Comparator comparator_9 (.a({func3, inst[14:12]}), .b(8'h7), .eq(comparator_9_eq));  // open: gt, lt
  Priority_Encoder #(.select(5)) priority_encoder_1 (
    .in15(addi[0]), .in16(slli[0]), .in17(slti[0]), .in18(xori[0]), .in19(srli[0]), .in20(srai[0]),
    .in21(ori[0]), .in22(andi[0]), .out(priority_encoder_1_out[4:0]));  // open: in0, in1, in2, in3, in4, in5, in6, in7, in8, in9, in10, in11, in12, in13, in14, in23, in24, in25, in26, in27, in28, in29, in30, in31, gs, en_out, en_in
  and and_1 (addi[0], i[0], comparator_2_eq);
  and and_2 (slli[0], i[0], comparator_3_eq);
  and and_3 (slti[0], i[0], comparator_4_eq);
  and and_4 (xori[0], i[0], comparator_5_eq);
  and and_5 (srli[0], i[0], comparator_6_eq);
  and and_6 (srai[0], i[0], comparator_7_eq);
  and and_7 (ori[0], i[0], comparator_8_eq);
  and and_8 (andi[0], i[0], comparator_9_eq);
  ROM #(.addrWidth(6), .dataWidth(16)) rom_1 (.addr(priority_encoder_1_out), .data(rom_1_data));
  // Pins of 2 and 7 and 8 bits meet at {opcode[7], inst[6:0]}
  // Pins of 2 and 3 and 8 bits meet at {func3, inst[14:12]}
  // Pins of 1 and 2 bits meet at i
  // Pins of 1 and 8 bits meet at addi
  // Pins of 1 and 8 bits meet at slli
  // Pins of 1 and 8 bits meet at slti
  // Pins of 1 and 8 bits meet at xori
  // Pins of 1 and 8 bits meet at srli
  // Pins of 1 and 8 bits meet at srai
  // Pins of 1 and 8 bits meet at ori
  // Pins of 1 and 8 bits meet at andi
  // Pins of 4 and 8 bits meet at {undriven, 4'b1011}

  // Other names for the same wires on the sheet: opcode[6:0] = inst[6:0]; func3[2:0] = inst[14:12]

  // Notes on the sheet:
  //   INPUTS to your circuit
  //   Connect ROM Input here ->
  //   contents of rom_1 (hex, n*v repeats v):
  //   4*9204 9224 9244 9284 92a4 93a4 92c4 92e4
  //   ROM FOR CONTROL LOGIC
  //   DON'T CHANGE THE LOCATIONS OF THE INPUTS AND OUTPUTS!
  //   OUTPUT from your circuit
  //   CLOSE
  //   WIRE
  //   TO
  //   USE
  //   ROM
  //   Reminder: Use combinational logic for PCSel
endmodule
