// Logisim project cpu.circ as structural Verilog: 1 circuit, main circuit cpu
module cpu (
  input  clk,
  input  [31:0] INSTRUCTION,
  input  [31:0] MEM_READ_DATA,
  output [31:0] MEM_WRITE_ADDRESS,
  output [31:0] PROGRAM_COUNTER,
  output [31:0] ra,
  output [31:0] sp,
  output [31:0] t0,
  output [31:0] t1,
  output [31:0] t2,
  output [31:0] s0,
  output [31:0] s1,
  output [31:0] a0,
  output [31:0] tohost,
  output [3:0] MEM_WRITE_ENABLE,
  output [31:0] MEM_WRITE_DATA
);

  wire ASel, BrEq, BrLt, BrUn, BSel, comparator_1_eq, comparator_2_eq, comparator_3_eq, comparator_5_eq,
       comparator_6_eq, comparator_7_eq, comparator_8_eq, CSRSel, CSRWen, is_i_type_load,
       is_i_type_load_store, is_lb, is_lh, is_lw, is_s_type_store, is_sb, is_sh, is_sw, MemRW, PCSel, RegWEn;
  wire [1:0] WBSel;
  wire [2:0] control_logic_1_immsel;
  wire [3:0] ALUSel;
  wire [7:0] and_4_out;
  wire [15:0] bit_extender_1_out;
  wire [31:0] ALUResult, imm, multiplexer_1_out, multiplexer_2_out, multiplexer_3_out, PC4, pc4_t,
       Read_Data_1, Read_Data_2, WBSelOutput;

  Adder #(.width(32)) adder_1 (.a(PROGRAM_COUNTER), .b(32'h4), .out(pc4_t));  // open: cin, cout
  Register #(.width(32)) PC (.D(multiplexer_1_out), .clk(clk), .Q(PROGRAM_COUNTER));  // open: en, clr
  Multiplexer #(.enable("false"), .width(32)) multiplexer_1 (
    .in0(pc4_t), .in1(ALUResult), .out(multiplexer_1_out), .sel(PCSel));
  control_logic control_logic_1 (
    .CSRWen(CSRWen), .PCSel(PCSel), .RegWEn(RegWEn), .ImmSel(control_logic_1_immsel), .BrUn(BrUn),
    .ASel(ASel), .BSel(BSel), .ALUSel(ALUSel), .MemRW(MemRW), .WBSel(WBSel), .CSRSel(CSRSel),
    .inst(INSTRUCTION), .BrEq(BrEq), .BrLt(BrLt));
  imm_gen imm_gen_1 (.inst(INSTRUCTION), .ImmSel(control_logic_1_immsel), .imm(imm));
  regfile regfile_1 (
    .rs1(INSTRUCTION[19:15]), .rs2(INSTRUCTION[24:20]), .rd(INSTRUCTION[11:7]), .Write_Data(WBSelOutput),
    .RegWEn(RegWEn), .clk(clk), .ra(ra), .sp(sp), .t0(t0), .t1(t1), .t2(t2), .s0(s0), .s1(s1), .a0(a0),
    .Read_Data_1(Read_Data_1), .Read_Data_2(Read_Data_2));
  branch_comp branch_comp_1 (.rs1(Read_Data_1), .rs2(Read_Data_2), .BrUn(BrUn), .BrEq(BrEq), .BrLt(BrLt));
  Multiplexer #(.enable("false"), .width(32)) multiplexer_2 (
    .in0(Read_Data_1), .in1(PROGRAM_COUNTER), .out(multiplexer_2_out), .sel(ASel));
  Multiplexer #(.enable("false"), .width(32)) multiplexer_3 (
    .in0(Read_Data_2), .in1(imm), .out(multiplexer_3_out), .sel(BSel));
  alu alu_1 (.Result(MEM_WRITE_ADDRESS), .A(multiplexer_2_out), .B(multiplexer_3_out), .ALUSel(ALUSel));
  // csr csr_1: pin names not known; wires that end beside it: tohost, is_i_type_load_store
  Comparator #(.width(3)) comparator_1 (.a(INSTRUCTION[14:12]), .b(3'b000), .eq(comparator_1_eq));  // open: gt, lt
  Comparator #(.width(3)) comparator_2 (.a(INSTRUCTION[14:12]), .b(3'b001), .eq(comparator_2_eq));  // open: gt, lt
  Comparator #(.width(3)) comparator_3 (.a(INSTRUCTION[14:12]), .b(3'b010), .eq(comparator_3_eq));  // open: gt, lt
  Comparator #(.width(7)) comparator_4 (.a(INSTRUCTION[6:0]), .b(7'b0000011), .eq(is_i_type_load));  // open: gt, lt
  and and_1 (is_lb, is_i_type_load, comparator_1_eq);
  and and_2 (is_lh, is_i_type_load, comparator_2_eq);
  and and_3 (is_lw, is_i_type_load, comparator_3_eq);
  Comparator #(.width(3)) comparator_5 (.a(INSTRUCTION[14:12]), .b(3'b000), .eq(comparator_5_eq));  // open: gt, lt
  Comparator #(.width(3)) comparator_6 (.a(INSTRUCTION[14:12]), .b(3'b001), .eq(comparator_6_eq));  // open: gt, lt
  Comparator #(.width(3)) comparator_7 (.a(INSTRUCTION[14:12]), .b(3'b010), .eq(comparator_7_eq));  // open: gt, lt
  and and_4 (and_4_out[0], is_lb, comparator_8_eq);
  Comparator comparator_8 (.eq(comparator_8_eq));  // open: a, b, gt, lt
  Comparator #(.width(7)) comparator_9 (.a(INSTRUCTION[6:0]), .b(7'b0100011), .eq(is_s_type_store));  // open: gt, lt
  and and_5 (is_sb, is_s_type_store, comparator_5_eq);
  and and_6 (is_sh, is_s_type_store, comparator_6_eq);
  and and_7 (is_sw, is_s_type_store, comparator_7_eq);
  assign bit_extender_1_out = {{8{and_4_out[7]}}, and_4_out};  // Bit_Extender bit_extender_1
  Multiplexer #(.enable("false"), .select(2), .width(32)) multiplexer_4 (
    .in0(MEM_READ_DATA), .in1(MEM_WRITE_ADDRESS), .in2(PC4), .out(WBSelOutput), .sel(WBSel));  // open: in3
  // Pins of 1 and 8 bits meet at and_4_out

  // Other names for the same wires on the sheet: alu_result[31:0] = MEM_WRITE_ADDRESS; opcode[6:0] = INSTRUCTION[6:0];
  //   rd[4:0] = INSTRUCTION[11:7]; func3[2:0] = INSTRUCTION[14:12]; rs1[4:0] = INSTRUCTION[19:15];
  //   rs2[4:0] = INSTRUCTION[24:20]

  // Notes on the sheet:
  //   Output to IMEM
  //   IMEM (do **NOT** move this)
  //   Inputs from IMEM
  //   It is OK to move the PC, RegFile, ALU, MEM, Branch Comp, Imm Gen, and Control Logic to wherever is most convenient for you when constructing your CPU, and to delete this text
  //   Inputs/Outputs for testing. Do **NOT** move these.
  //   Outputs To DMEM
  //   DMEM (do **NOT** move this)
  //   Inputs From DMEM
endmodule
