// Logisim project imm-gen.circ as structural Verilog: 1 circuit, main circuit imm_gen
module imm_gen (
  input  [31:0] inst,
  input  [2:0] ImmSel,
  output [31:0] imm
);

  wire [0:0] immediate_sb;
  wire [31:0] imm_csr, imm_i, imm_sb, imm_store;

  assign imm_i = {{20{inst[31]}}, inst[31:20]};  // Bit_Extender bit_extender_1
  assign imm_sb = {{19{inst[31]}}, {inst[31], inst[7], inst[30:25], inst[11:8], immediate_sb[0]}};  // Bit_Extender bit_extender_2
  assign imm_store = {{20{inst[31]}}, {inst[31:25], inst[11:7]}};  // Bit_Extender bit_extender_3
  assign imm_csr = {{20{inst[31]}}, inst[31:20]};  // Bit_Extender bit_extender_4
  Multiplexer #(.enable("false"), .select(3), .width(32)) multiplexer_1 (
    .in1(imm_i), .in2(imm_store), .in3(imm_sb), .in7(imm_csr), .out(imm), .sel(ImmSel));  // open: in0, in4, in5, in6

  // Other names for the same wires on the sheet: immediate_sb[12:1] = {inst[31], inst[7], inst[30:25], inst[11:8]};
  //   immediate_store[11:0] = {inst[31:25], inst[11:7]}; immediate_csr[11:0] = inst[31:20];
  //   immediate_i[11:0] = inst[31:20]

  // Notes on the sheet:
  //   INPUTS to your circuit
  //   DON'T CHANGE THE LOCATIONS OF THE INPUTS AND OUTPUTS!
  //   OUTPUT from your circuit
endmodule
